# Fritzing sketch ECAD (saved by Fritzing 0.9.3b)
breadboards: 1

parts:
  LCD1 = LCD screen
  Part1 = Arduino Uno (Rev3)
  U1 = POT_SWITCH [package=pot_pth]
  J1 = Piezo Speaker
  LED1 = smd LED [color="Red (633nm)" package="0603 [SMD]"]
  R1 = Resistor [tolerance=±5% resistance=220 package=THT]
  Part2 = HC-SR501 Body Sensor Module

nets:
  GND: LCD1.VSS, LCD1.R/W, LCD1.LED-, Part1.GND, U1.G$1_E, J1.pin1, LED1.cathode, Part2.GND
  VDD: LCD1.VDD, LCD1.LED+, Part1.5V, U1.G$1_A, Part2.VCC
  N1: LCD1.V0, U1.G$2_1
  N2: LCD1.RS, Part1.D12/MISO
  N3: LCD1.E, Part1.D2
  N4: LCD1.DB4, Part1.D4
  N5: LCD1.DB5, Part1.D5_PWM
  N6: LCD1.DB6, Part1.D6_PWM
  N7: LCD1.DB7, Part1.D7
  N8: Part1.D8, J1.pin2, R1.Pin_1
  N9: Part1.D13/SCK, Part2.OUT
  N10: LED1.anode, R1.Pin_0

custom parts:
  HC-SR501 Body Sensor Module: Pyroelectric Infrared PIR Motion Sensor Detector Module
